# Fritzing sketch adu01 (saved by Fritzing 0.9.3b)
breadboards: 1

parts:
  부품1 = Arduino Uno (Rev3) - ICSP
  LED1 = smd LED [color="Red (633nm)" package="1206 [SMD]"]
  R1 = Resistor [tolerance=±5% resistance=220 package=THT]

nets:
  N1: 부품1.GND, R1.Pin_0
  N2: 부품1.D2, LED1.anode
  N3: LED1.cathode, R1.Pin_1

// code stored in the sketch: blink.ino
#define LED_PIN 2
#define HIGH_TIME 1000
#define LOW_TIME 500

void setup() {
  // put your setup code here, to run once:
  pinMode(LED_PIN, OUTPUT);
}

void loop() {
  // put your main code here, to run repeatedly:
  digitalWrite(LED_PIN, HIGH);
  delay(HIGH_TIME);
  digitalWrite(LED_PIN, LOW);
  delay(OW_TIME);
}
